// Logisim project 7BitRegister.circ as structural Verilog: 1 circuit, main circuit main
module main (
  input  [6:0] in_1,
  input  ld,
  input  clr,
  input  clk,
  output [6:0] out_5
);

  Register #(.width(7)) register_1 (.D(in_1), .en(ld), .Q(out_5), .clk(clk), .clr(clr));
endmodule
