// Logisim project ALU.circ as structural Verilog: 1 circuit, main circuit main
module main (
  input  [10:0] Op,
  input  [15:0] DR,
  input  CLK,
  output [15:0] out,
  output Overflow,
  output Underflow
);

  wire main_16_cout, main_16_inco, or_1_out;
  wire [2:0] main_1_bout, main_2_bout, main_3_bout, main_4_bout, main_5_bout, main_6_bout, main_7_bout,
       main_8_bout, main_9_bout, main_10_bout, main_11_bout, main_12_bout, main_13_bout, main_14_bout,
       main_15_bout;

  or or_1 (or_1_out, Op[0], Op[1], Op[2], Op[3], Op[4], Op[5], Op[6], Op[7], Op[8], Op[9], Op[10]);
  alublock_main main_1 (
    .in_7(Op), .DR_i(DR[0]), .AC_i_1(out[15]), .AC_i_1_2(out[1]), .IncC(1'b1), .Cin(1'b0), .Bin(1'b0),
    .LD(or_1_out), .IncO(main_1_bout[2]), .Cout(main_1_bout[1]), .Bout(main_1_bout[0]), .clk(CLK),
    .out(out[0]));  // open: AC_i
  alublock_main main_2 (
    .in_7(Op), .DR_i(DR[1]), .AC_i_1(out[0]), .AC_i_1_2(out[2]), .IncC(main_1_bout[2]), .Cin(main_1_bout[1]),
    .Bin(main_1_bout[0]), .LD(or_1_out), .IncO(main_2_bout[2]), .Cout(main_2_bout[1]), .Bout(main_2_bout[0]),
    .clk(CLK), .out(out[1]));  // open: AC_i
  alublock_main main_3 (
    .in_7(Op), .DR_i(DR[2]), .AC_i_1(out[1]), .AC_i_1_2(out[3]), .IncC(main_2_bout[2]), .Cin(main_2_bout[1]),
    .Bin(main_2_bout[0]), .LD(or_1_out), .IncO(main_3_bout[2]), .Cout(main_3_bout[1]), .Bout(main_3_bout[0]),
    .clk(CLK), .out(out[2]));  // open: AC_i
  alublock_main main_4 (
    .in_7(Op), .DR_i(DR[3]), .AC_i_1(out[2]), .AC_i_1_2(out[5]), .IncC(main_3_bout[2]), .Cin(main_3_bout[1]),
    .Bin(main_3_bout[0]), .LD(or_1_out), .IncO(main_4_bout[2]), .Cout(main_4_bout[1]), .Bout(main_4_bout[0]),
    .clk(CLK), .out(out[3]));  // open: AC_i
  alublock_main main_5 (
    .in_7(Op), .DR_i(DR[4]), .AC_i_1(out[3]), .AC_i_1_2(out[5]), .IncC(main_4_bout[2]), .Cin(main_4_bout[1]),
    .Bin(main_4_bout[0]), .LD(or_1_out), .IncO(main_5_bout[2]), .Cout(main_5_bout[1]), .Bout(main_5_bout[0]),
    .clk(CLK), .out(out[4]));  // open: AC_i
  alublock_main main_6 (
    .in_7(Op), .DR_i(DR[5]), .AC_i_1(out[4]), .AC_i_1_2(out[6]), .IncC(main_5_bout[2]), .Cin(main_5_bout[1]),
    .Bin(main_5_bout[0]), .LD(or_1_out), .IncO(main_6_bout[2]), .Cout(main_6_bout[1]), .Bout(main_6_bout[0]),
    .clk(CLK), .out(out[5]));  // open: AC_i
  alublock_main main_7 (
    .in_7(Op), .DR_i(DR[6]), .AC_i_1(out[5]), .AC_i_1_2(out[8]), .IncC(main_6_bout[2]), .Cin(main_6_bout[1]),
    .Bin(main_6_bout[0]), .LD(or_1_out), .IncO(main_7_bout[2]), .Cout(main_7_bout[1]), .Bout(main_7_bout[0]),
    .clk(CLK), .out(out[6]));  // open: AC_i
  alublock_main main_8 (
    .in_7(Op), .DR_i(DR[7]), .AC_i_1(out[6]), .AC_i_1_2(out[8]), .IncC(main_7_bout[2]), .Cin(main_7_bout[1]),
    .Bin(main_7_bout[0]), .LD(or_1_out), .IncO(main_8_bout[2]), .Cout(main_8_bout[1]), .Bout(main_8_bout[0]),
    .clk(CLK), .out(out[7]));  // open: AC_i
  alublock_main main_9 (
    .in_7(Op), .DR_i(DR[8]), .AC_i_1(out[7]), .AC_i_1_2(out[9]), .IncC(main_8_bout[2]), .Cin(main_8_bout[1]),
    .Bin(main_8_bout[0]), .LD(or_1_out), .IncO(main_9_bout[2]), .Cout(main_9_bout[1]), .Bout(main_9_bout[0]),
    .clk(CLK), .out(out[8]));  // open: AC_i
  alublock_main main_10 (
    .in_7(Op), .DR_i(DR[9]), .AC_i_1(out[8]), .AC_i_1_2(out[11]), .IncC(main_9_bout[2]),
    .Cin(main_9_bout[1]), .Bin(main_9_bout[0]), .LD(or_1_out), .IncO(main_10_bout[2]),
    .Cout(main_10_bout[1]), .Bout(main_10_bout[0]), .clk(CLK), .out(out[9]));  // open: AC_i
  alublock_main main_11 (
    .in_7(Op), .DR_i(DR[10]), .AC_i_1(out[9]), .AC_i_1_2(out[11]), .IncC(main_10_bout[2]),
    .Cin(main_10_bout[1]), .Bin(main_10_bout[0]), .LD(or_1_out), .IncO(main_11_bout[2]),
    .Cout(main_11_bout[1]), .Bout(main_11_bout[0]), .clk(CLK), .out(out[10]));  // open: AC_i
  alublock_main main_12 (
    .in_7(Op), .DR_i(DR[11]), .AC_i_1(out[10]), .AC_i_1_2(out[12]), .IncC(main_11_bout[2]),
    .Cin(main_11_bout[1]), .Bin(main_11_bout[0]), .LD(or_1_out), .IncO(main_12_bout[2]),
    .Cout(main_12_bout[1]), .Bout(main_12_bout[0]), .clk(CLK), .out(out[11]));  // open: AC_i
  alublock_main main_13 (
    .in_7(Op), .DR_i(DR[12]), .AC_i_1(out[11]), .AC_i_1_2(out[14]), .IncC(main_12_bout[2]),
    .Cin(main_12_bout[1]), .Bin(main_12_bout[0]), .LD(or_1_out), .IncO(main_13_bout[2]),
    .Cout(main_13_bout[1]), .Bout(main_13_bout[0]), .clk(CLK), .out(out[12]));  // open: AC_i
  alublock_main main_14 (
    .in_7(Op), .DR_i(DR[13]), .AC_i_1(out[12]), .AC_i_1_2(out[14]), .IncC(main_13_bout[2]),
    .Cin(main_13_bout[1]), .Bin(main_13_bout[0]), .LD(or_1_out), .IncO(main_14_bout[2]),
    .Cout(main_14_bout[1]), .Bout(main_14_bout[0]), .clk(CLK), .out(out[13]));  // open: AC_i
  alublock_main main_15 (
    .in_7(Op), .DR_i(DR[14]), .AC_i_1(out[13]), .AC_i_1_2(out[15]), .IncC(main_14_bout[2]),
    .Cin(main_14_bout[1]), .Bin(main_14_bout[0]), .LD(or_1_out), .IncO(main_15_bout[2]),
    .Cout(main_15_bout[1]), .Bout(main_15_bout[0]), .clk(CLK), .out(out[14]));  // open: AC_i
  alublock_main main_16 (
    .in_7(Op), .DR_i(DR[15]), .AC_i_1(out[14]), .AC_i_1_2(out[0]), .IncC(main_15_bout[2]),
    .Cin(main_15_bout[1]), .Bin(main_15_bout[0]), .LD(or_1_out), .IncO(main_16_inco), .Cout(main_16_cout),
    .Bout(Underflow), .clk(CLK), .out(out[15]));  // open: AC_i
  or or_2 (Overflow, main_16_cout, main_16_inco);
endmodule
