// Logisim project DecodeMicropLogic.circ as structural Verilog: 1 circuit, main circuit main
module main (
  input  [2:0] f1,
  input  [2:0] f2,
  input  [2:0] f3,
  output ADD,
  output clr_AC,
  output inc_AC,
  output ld_AC,
  output ld_ARfDR,
  output ld_ARfPC,
  output Write,
  output SUB,
  output OR,
  output AND,
  output Read___mux1,
  output ld_DRfAC____mux2,
  output inc_DR,
  output ld_DRfPC____mux0,
  output XOR,
  output COM,
  output SHL,
  output SHR,
  output inc_PC,
  output ld_PC,
  output Reserved
);

  Decoder #(.select(3)) decoder_1 (
    .out1(ADD), .out2(clr_AC), .out3(inc_AC), .out4(ld_AC), .out5(ld_ARfDR), .out6(ld_ARfPC), .out7(Write),
    .sel(f1));  // open: out0, en
  Decoder #(.select(3)) decoder_2 (
    .out1(SUB), .out2(OR), .out3(AND), .out4(Read___mux1), .out5(ld_DRfAC____mux2), .out6(inc_DR),
    .out7(ld_DRfPC____mux0), .sel(f2));  // open: out0, en
  Decoder #(.select(3)) decoder_3 (
    .out1(XOR), .out2(COM), .out3(SHL), .out4(SHR), .out5(inc_PC), .out6(ld_PC), .out7(Reserved), .sel(f3));  // open: out0, en
endmodule
