// Logisim project MAIN CIRCUIT.circ as structural Verilog: 1 circuit, main circuit main
module main (
  output O,
  output U
);

  wire Clock_out, F1_F2_F3_inc_dr, F1_F2_F3_ld_drfac____mux2, F1_F2_F3_ld_drfpc____mux0, or_1_out, or_2_out,
       undriven;
  wire [1:0] F1_F2_F3_inc_pc, F1_F2_F3_ld_arfdr, F1_F2_F3_write, priority_encoder_1_p3;
  wire [2:0] Sequencer_car_2, Sequencer_f1, Sequencer_f2, Sequencer_f3;
  wire [3:0] PC_out_6, PC_out_6_2, Sequencer_car;
  wire [4:0] DR_out_6_2;
  wire [6:0] Sequencer_sbr;
  wire [10:0] AR_out_6, DR_out_6, F1_F2_F3_add, multiplexer_1_out;
  wire [10:8] PC_out_6_3;
  wire [15:0] main_1_out, multiplexer_2_out, RAM_out_6;

  Multiplexer #(.width(11)) multiplexer_1 (
    .in0({PC_out_6_3, PC_out_6_2, PC_out_6}), .in1(DR_out_6), .out(multiplexer_1_out),
    .sel(F1_F2_F3_ld_arfdr[0]), .en(undriven));
  or or_1 (or_1_out, F1_F2_F3_ld_arfdr[1], F1_F2_F3_ld_arfdr[0]);
  _11BitRegister_main AR (
    .in_1(multiplexer_1_out), .Increment(1'b0), .ld(or_1_out), .clr(1'b0), .out_6(AR_out_6), .clk(Clock_out));
  _11BitRegister_main PC (
    .in_1(AR_out_6), .Increment(F1_F2_F3_inc_pc[0]), .ld(F1_F2_F3_inc_pc[1]),
    .out_6({PC_out_6_3, PC_out_6_2, PC_out_6}), .clk(Clock_out));  // open: clr
  main_main Sequencer (
    .AC(main_1_out), .DR({DR_out_6_2, DR_out_6}), .F1(Sequencer_f1), .F2(Sequencer_f2), .F3(Sequencer_f3),
    .CLK(Clock_out), .SBR(Sequencer_sbr), .CAR({Sequencer_car_2, Sequencer_car}));
  DecodeMicropLogic_main F1_F2_F3 (
    .f1(Sequencer_f1), .f2(Sequencer_f2), .f3(Sequencer_f3), .ADD(F1_F2_F3_add[0]), .clr_AC(F1_F2_F3_add[1]),
    .inc_AC(F1_F2_F3_add[2]), .ld_AC(F1_F2_F3_add[3]), .ld_ARfDR(F1_F2_F3_ld_arfdr[0]),
    .ld_ARfPC(F1_F2_F3_ld_arfdr[1]), .Write(F1_F2_F3_write[0]), .SUB(F1_F2_F3_add[4]), .OR(F1_F2_F3_add[5]),
    .AND(F1_F2_F3_add[6]), .Read___mux1(F1_F2_F3_write[1]), .ld_DRfAC____mux2(F1_F2_F3_ld_drfac____mux2),
    .inc_DR(F1_F2_F3_inc_dr), .ld_DRfPC____mux0(F1_F2_F3_ld_drfpc____mux0), .XOR(F1_F2_F3_add[7]),
    .COM(F1_F2_F3_add[8]), .SHL(F1_F2_F3_add[9]), .SHR(F1_F2_F3_add[10]), .inc_PC(F1_F2_F3_inc_pc[0]),
    .ld_PC(F1_F2_F3_inc_pc[1]));  // open: Reserved
  // Priority_Encoder #(.select(2)) priority_encoder_1: pin names not known; wires that end beside it: F1_F2_F3_ld_drfpc____mux0, F1_F2_F3_write[1], priority_encoder_1_p3, F1_F2_F3_ld_drfac____mux2, 1'b0
  or or_2 (or_2_out, F1_F2_F3_ld_drfpc____mux0, F1_F2_F3_write[1], F1_F2_F3_ld_drfac____mux2);
  Ram2048X16_main RAM (
    .address(AR_out_6), .data({DR_out_6_2, DR_out_6}), .WRITE(F1_F2_F3_write[0]), .READ(F1_F2_F3_write[1]),
    .out_6(RAM_out_6), .CLK(Clock_out));
  Multiplexer #(.select(2), .width(16)) multiplexer_2 (
    .in0({{5{1'b0}}, PC_out_6_3, PC_out_6_2, PC_out_6}), .in1(RAM_out_6), .in2(main_1_out),
    .out(multiplexer_2_out), .sel(priority_encoder_1_p3));  // open: in3, en
  _16BitRegister_main DR (
    .in_1(multiplexer_2_out), .Increment(F1_F2_F3_inc_dr), .ld(or_2_out), .out_6({DR_out_6_2, DR_out_6}),
    .clk(Clock_out));  // open: clr
  Clock Clock (.out(Clock_out));
  ALU_main main_1 (
    .Op(F1_F2_F3_add), .CLK(Clock_out), .DR({DR_out_6_2, DR_out_6}), .out(main_1_out), .Overflow(O),
    .Underflow(U));
  Hex_Digit_Display hex_digit_display_1 (.value(main_1_out[15:12]));  // open: dp
  Hex_Digit_Display hex_digit_display_2 (.value(main_1_out[11:8]));  // open: dp
  Hex_Digit_Display hex_digit_display_3 (.value(main_1_out[15:12]));  // open: dp
  Hex_Digit_Display hex_digit_display_4 (.value(main_1_out[11:8]));  // open: dp
  Hex_Digit_Display hex_digit_display_5 (.value({AR_out_6[10:8], 1'b0}));  // open: dp
  Hex_Digit_Display hex_digit_display_6 (.value(AR_out_6[7:4]));  // open: dp
  Hex_Digit_Display hex_digit_display_7 (.value(main_1_out[3:0]));  // open: dp
  Hex_Digit_Display hex_digit_display_8 (.value(main_1_out[7:4]));  // open: dp
  Hex_Digit_Display hex_digit_display_9 (.value(main_1_out[7:4]));  // open: dp
  Hex_Digit_Display hex_digit_display_10 (.value(main_1_out[3:0]));  // open: dp
  Hex_Digit_Display hex_digit_display_11 (.value(AR_out_6[3:0]));  // open: dp
  Hex_Digit_Display hex_digit_display_12 (.value({PC_out_6_3, 1'b0}));  // open: dp
  Hex_Digit_Display hex_digit_display_13 (.value({1'b0, Sequencer_sbr[6:4]}));  // open: dp
  Hex_Digit_Display hex_digit_display_14 (.value(Sequencer_sbr[3:0]));  // open: dp
  Hex_Digit_Display hex_digit_display_15 (.value(PC_out_6_2));  // open: dp
  Hex_Digit_Display hex_digit_display_16 (.value({1'b0, Sequencer_car_2}));  // open: dp
  Hex_Digit_Display hex_digit_display_17 (.value(PC_out_6));  // open: dp
  Hex_Digit_Display hex_digit_display_18 (.value(Sequencer_car));  // open: dp

  // Notes on the sheet:
  //   Computer 2
  //   AR
  //   DR
  //   AC
  //   SBR
  //   PC
  //   CAR
endmodule
