// Logisim project Ram2048X16.circ as structural Verilog: 1 circuit, main circuit main
module main (
  input  [10:0] address,
  input  [15:0] data,
  input  WRITE,
  input  READ,
  input  CLK,
  output [15:0] out_6
);

  RAM #(.addrWidth(11), .dataWidth(16), .bus("separate")) ram_1 (
    .addr(address), .din(data), .data(out_6), .str(WRITE), .clk(CLK), .ld(READ));  // open: sel, clr
endmodule
