// Logisim project alublock.circ as structural Verilog: 1 circuit, main circuit main
module main (
  input  DR_i,
  input  AC_i_1,
  input  AC_i_1_2,
  input  IncC,
  input  Cin,
  input  Bin,
  input  [10:0] in_7,
  input  LD,
  input  clk,
  output AC_i,
  output Cout,
  output IncO,
  output out,
  output Bout
);

  wire ADD_out, adder_1_out, adder_2_out, and_1_out, AND_2_out, CLR_out, COM_out, DR_out, INC_out, not_1_out,
       not_2_out, not_3_out, or_1_out, OR_2_out, or_3_out, SHL_out, SHR_out, SUB_out, subtractor_1_out,
       xor_1_out, XOR_2_out;

  or or_1 (or_1_out, AC_i, DR_i);
  and and_1 (and_1_out, AC_i, DR_i);
  not not_1 (not_1_out, AC_i);
  Adder #(.width(1)) adder_1 (.a(AC_i), .b(DR_i), .out(adder_1_out), .cin(Cin), .cout(Cout));
  not not_2 (not_2_out, in_7[1]);
  Adder #(.width(1)) adder_2 (.a(AC_i), .b(1'b0), .out(adder_2_out), .cin(IncC), .cout(IncO));
  Subtractor #(.width(1)) subtractor_1 (.a(AC_i), .b(DR_i), .out(subtractor_1_out), .bin(Bin), .bout(Bout));
  xor xor_1 (xor_1_out, AC_i, DR_i);
  and ADD (ADD_out, in_7[0], adder_1_out);
  and CLR (CLR_out, in_7[1], not_2_out);
  and INC (INC_out, in_7[2], adder_2_out);
  and DR (DR_out, in_7[3], DR_i);
  and SUB (SUB_out, in_7[4], subtractor_1_out);
  and OR_2 (OR_2_out, in_7[5], or_1_out);
  and AND_2 (AND_2_out, in_7[6], and_1_out);
  and XOR_2 (XOR_2_out, in_7[7], xor_1_out);
  and COM (COM_out, in_7[8], not_1_out);
  and SHL (SHL_out, in_7[9], AC_i_1);
  and SHR (SHR_out, in_7[10], AC_i_1_2);
  or or_3 (or_3_out, ADD_out, CLR_out, INC_out, DR_out, SUB_out, OR_2_out, AND_2_out, XOR_2_out, COM_out, SHL_out, SHR_out);
  not not_3 (not_3_out, or_3_out);
  J_K_Flip_Flop j_k_ff_1 (.J(or_3_out), .clk(clk), .K(not_3_out), .Q(AC_i), .en(LD));  // open: Qn, preset, reset

  assign out = AC_i;
endmodule
