// Logisim project main.circ as structural Verilog: 1 circuit, main circuit main
module main (
  input  [15:0] AC,
  input  [15:0] DR,
  input  CLK,
  output [6:0] SBR,
  output [6:0] CAR,
  output [2:0] F1,
  output [2:0] F2,
  output [2:0] F3
);

  wire main_1_ld, multiplexer_1_out, or_1_out;
  wire [1:0] main_1_s0, rom_1_data_2;
  wire [6:0] adder_1_out, multiplexer_2_out, rom_1_data;
  wire [10:9] rom_1_data_3;

  or or_1 (or_1_out, AC[15], AC[14], AC[13], AC[12], AC[11], AC[10], AC[9], AC[8], AC[7], AC[6], AC[5], AC[4], AC[3], AC[2], AC[1], AC[0], AC[0]);
  InputLogicMicroprogram_main main_1 (
    .I1(rom_1_data_2[1]), .I0(rom_1_data_2[0]), .T(multiplexer_1_out), .S1(main_1_s0[1]), .S0(main_1_s0[0]),
    .LD(main_1_ld));
  Multiplexer #(.select(2)) multiplexer_1 (
    .in0(1'b1), .in1(DR[15]), .in2(AC[15]), .in3(or_1_out), .out(multiplexer_1_out), .sel(rom_1_data_3));  // open: en
  Multiplexer #(.select(2), .width(7)) multiplexer_2 (
    .in0(adder_1_out), .in1(rom_1_data), .in2(SBR), .in3({1'b0, DR[14:11], 2'b00}), .out(multiplexer_2_out),
    .sel(main_1_s0));  // open: en
  _7BitRegister_main u_CAR (.in_1(multiplexer_2_out), .ld(1'b1), .clk(CLK), .out_5(CAR));  // open: clr
  Adder #(.width(7)) adder_1 (.a(7'b0000001), .b(CAR), .out(adder_1_out));  // open: cin, cout
  ROM #(.addrWidth(7), .dataWidth(20)) rom_1 (
    .addr(CAR), .data({F1, F2, F3, rom_1_data_3, rom_1_data_2, rom_1_data}));  // open: sel
  _7BitRegister_main u_SBR (.in_1(adder_1_out), .ld(main_1_ld), .clk(CLK), .out_5(SBR));  // open: clr

  // Notes on the sheet:
  //   contents of rom_1 (hex, n*v repeats v):
  //   10224
endmodule
